// Logisim project grnMem1.circ as structural Verilog: 1 circuit, main circuit grnMem1
module grnMem1 (
  input  [5:0] in_1,
  output [3:0] out_2
);

  ROM #(.addrWidth(6), .dataWidth(4)) rom_1 (.addr(in_1), .data(out_2));  // open: sel

  // Notes on the sheet:
  //   contents of rom_1 (hex, n*v repeats v):
  //   4*b 4*2 9*b 10*2 b 6*2 10*b 2 8*b
endmodule
