// Logisim project grnMem2.circ as structural Verilog: 1 circuit, main circuit grnMem2
module grnMem2 (
  input  [5:0] in_1,
  output [31:0] out_2
);

  ROM #(.addrWidth(6), .dataWidth(32)) rom_1 (.addr(in_1), .data(out_2));  // open: sel

  // Notes on the sheet:
  //   contents of rom_1 (hex, n*v repeats v):
  //   700f011 80013a1 80013a2 80813a1 204e860 204e861 204e862 204e863 80813a2 80813a3 80813a4 80813a5
  //   80813a6 80813a7 80813a8 80813a9 82813a1 a04e860 a04e861 a04e862 a04e863 a04e864 a04e865 a04e866
  //   a04e867 a04e868 a04e869 82813a2 a04e8a0 a04e8a1 a04e8a2 a04e8a3 a04e8a4 a04e8a5 82813a3 82813a4
  //   82813a5 82813a6 82813a7 82813a8 82813a9 83013a1 83013a2 83413a1 d04e860 83413a2 83413a3 83413a4
  //   83413a5 83413a6 83413a7 83413a8 83413a9
endmodule
